# Fritzing sketch dubNodeMCU-WaterTank (saved by Fritzing 0.9.3b)
breadboards: 1

parts:
  U1 = NodeMCU V1.0
  Part1 = Barometric Pressure Sensor - BMP180 Breakout (GY-68)
  hc-sr1 = hc-sr04
  RHT1 = Humidity and Temperature Sensor RHT03

nets:
  N1: U1.D1, Part1.SCL
  N2: U1.D2, Part1.SDA
  N3: U1.D3, RHT1.Data-signal
  VCC: U1.3V3, Part1.VCC, RHT1.Vcc
  GND: U1.GND, Part1.GND, hc-sr1.GND, RHT1.GND_1
  N4: U1.D5, hc-sr1.Echo
  N5: U1.D6, hc-sr1.Trig
  VIN: U1.Vin, hc-sr1.VCC

custom parts:
  NodeMCU V1.0: ESP9266 based NodeMCU
